# Fritzing sketch temperature (saved by Fritzing 0.9.2b)
breadboards: 1

parts:
  Part1 = Arduino Uno (Rev3)
  R1 = Resistor [tolerance=±5% resistance=1k package="0402 [SMD]"]
  R2 = Resistor [tolerance=±5% resistance=1k package="0402 [SMD]"]
  T1 = LM35 Temperature Sensor [package="TO92 [THT]"]

nets:
  N1: Part1.A0, R1.Pin_0, T1.Vout
  N2: Part1.5V, R2.Pin_1
  GND: Part1.GND, T1.GND
  N3: R1.Pin_1, R2.Pin_0
